// Logisim project hw4.circ as structural Verilog
module ALU (
  input  [2:0] OpType,
  input  [15:0] op1,
  input  [15:0] op2,
  input  [15:0] OutputData,
  input  [2:0] shamt
);

  wire [3:0] bit_extender_1_out;
  wire [15:0] adder_1_out, or_1_out, shifter_1_out, shifter_2_out, subtractor_1_out, xor_1_out;

  assign bit_extender_1_out = {{1{1'b0}}, shamt};  // Bit_Extender bit_extender_1
  main main_1 ();
  Adder #(.width(16)) adder_1 (.a(op1), .b(op2), .out(adder_1_out));  // open: cin, cout
  Subtractor #(.width(16)) subtractor_1 (.a(op1), .b(op2), .out(subtractor_1_out));  // open: bin, bout
  assign or_1_out = op1 | op2;  // OR_Gate or_1, 16 bits wide
  assign xor_1_out = op1 ^ op2;  // XOR_Gate xor_1, 16 bits wide
  Shifter #(.width(16)) shifter_1 (.\dist (bit_extender_1_out), .out(shifter_1_out));  // open: in
  Shifter #(.width(16), .shift("ar")) shifter_2 (.\dist (bit_extender_1_out), .out(shifter_2_out));  // open: in
  Multiplexer #(.select(3), .width(16), .enable("false")) multiplexer_1 (
    .in0(adder_1_out), .in1(subtractor_1_out), .in2(or_1_out), .in3(xor_1_out), .in4(shifter_1_out),
    .in5(shifter_2_out), .out(OutputData), .sel(OpType));  // open: in6, in7

  // Other names for the same wires on the sheet: OT[2:0] = OpType
endmodule
